// Logisim project schem.circ as structural Verilog: 1 circuit, main circuit main
module main (
  input  a,
  input  b,
  input  c,
  input  d
);

  wire NAND_1_out, NAND_2_out, NAND_3_out, NAND_4_out, not_1_out;

  not not_1 (not_1_out, b);
  nand NAND_1 (NAND_1_out, a, not_1_out);
  nand NAND_2 (NAND_2_out, a, c);
  nand NAND_3 (NAND_3_out, NAND_2_out, b);
  nand NAND_4 (NAND_4_out, NAND_1_out, NAND_3_out);
  LED OUT_1 (.in(NAND_4_out));
endmodule
