// Logisim project schem2.circ as structural Verilog: 1 circuit, main circuit main
module main (
  input  a,
  input  b,
  input  c,
  input  d
);

  wire NOR_1_out, NOR_2_out, NOR_3_out, NOR_4_out, not_1_out, not_2_out, not_3_out, not_4_out, not_5_out;

  not not_1 (not_1_out, a);
  not not_2 (not_2_out, b);
  not not_3 (not_3_out, c);
  not not_4 (not_4_out, not_2_out);
  nor NOR_1 (NOR_1_out, not_1_out, not_3_out);
  nor NOR_2 (NOR_2_out, not_1_out, not_4_out);
  nor NOR_3 (NOR_3_out, not_2_out, NOR_1_out);
  nor NOR_4 (NOR_4_out, NOR_3_out, NOR_2_out);
  not not_5 (not_5_out, NOR_4_out);
  LED OUT_1 (.in(not_5_out));
endmodule
