// Logisim project schem.circ as structural Verilog: 1 circuit, main circuit main
module main (
  input  Z
);

  wire clk_out, d_ff_1_q, d_ff_1_qn, d_ff_2_q, d_ff_2_qn, d_ff_3_q, d_ff_3_qn, nand_1_out, nand_2_out,
       nand_3_out, nand_4_out, nand_5_out, nand_6_out, nand_7_out, nand_8_out, nand_9_out, nor_1_out,
       not_1_out, reset_out;

  not not_1 (not_1_out, Z);
  nand nand_1 (nand_1_out, not_1_out, d_ff_2_qn);
  nand nand_2 (nand_2_out, d_ff_3_qn, d_ff_2_q, Z);
  nand nand_3 (nand_3_out, not_1_out, d_ff_2_q, d_ff_3_qn);
  nand nand_4 (nand_4_out, Z, d_ff_3_q);
  nand nand_5 (nand_5_out, not_1_out, d_ff_2_q);
  nand nand_6 (nand_6_out, d_ff_1_qn, d_ff_2_qn, d_ff_3_qn, Z);
  nand nand_7 (nand_7_out, nand_1_out, nand_2_out, d_ff_1_qn);
  nand nand_8 (nand_8_out, nand_3_out, nand_4_out);
  nand nand_9 (nand_9_out, nand_5_out, nand_6_out);
  Button clk (.out(clk_out));
  D_Flip_Flop d_ff_1 (.D(nand_7_out), .clk(clk_out), .Q(d_ff_1_q), .Qn(d_ff_1_qn), .reset(reset_out));  // open: preset
  D_Flip_Flop d_ff_2 (.D(nand_8_out), .clk(clk_out), .Q(d_ff_2_q), .Qn(d_ff_2_qn), .reset(reset_out));  // open: preset
  D_Flip_Flop d_ff_3 (.D(nand_9_out), .clk(clk_out), .Q(d_ff_3_q), .Qn(d_ff_3_qn), .reset(reset_out));  // open: preset
  Button reset (.out(reset_out));
  LED Q2 (.in(d_ff_1_q));
  LED Q1 (.in(d_ff_2_q));
  LED Q0 (.in(d_ff_3_q));
  LED Y (.in(nor_1_out));
  nor nor_1 (nor_1_out, d_ff_3_q, d_ff_2_qn);
endmodule
