// Logisim project schem.circ as structural Verilog: 1 circuit, main circuit main
module main (
  input  Z,
  input  P
);

  wire clk_out, d_ff_1_q, d_ff_1_qn, d_ff_2_q, d_ff_2_qn, nand_1_out, nand_2_out, nand_3_out, nand_4_out,
       nand_5_out, nand_6_out, nand_7_out, nand_8_out, nand_9_out, nand_10_out, not_1_out, not_2_out,
       reset_out;

  not not_1 (not_1_out, P);
  not not_2 (not_2_out, Z);
  Button clk (.out(clk_out));
  Button reset (.out(reset_out));
  nand nand_1 (nand_1_out, Z, d_ff_2_q);
  nand nand_2 (nand_2_out, P, d_ff_1_q, not_2_out);
  D_Flip_Flop d_ff_1 (.D(nand_3_out), .clk(clk_out), .Q(d_ff_1_q), .Qn(d_ff_1_qn), .reset(reset_out));  // open: preset
  nand nand_3 (nand_3_out, nand_1_out, nand_2_out);
  LED Q0 (.in(d_ff_2_q));
  LED Q1 (.in(d_ff_1_q));
  nand nand_4 (nand_4_out, d_ff_1_q, P);
  nand nand_5 (nand_5_out, d_ff_2_q, not_1_out);
  nand nand_6 (nand_6_out, Z, d_ff_1_qn, d_ff_2_qn);
  nand nand_7 (nand_7_out, not_1_out, not_2_out, d_ff_2_q);
  nand nand_8 (nand_8_out, not_1_out, not_2_out, d_ff_1_q);
  nand nand_9 (nand_9_out, nand_4_out, nand_5_out);
  D_Flip_Flop d_ff_2 (.D(nand_10_out), .clk(clk_out), .Q(d_ff_2_q), .Qn(d_ff_2_qn), .reset(reset_out));  // open: preset
  nand nand_10 (nand_10_out, nand_6_out, nand_7_out, nand_8_out);
  LED Y (.in(nand_9_out));
endmodule
