// Logisim project schem.circ as structural Verilog: 1 circuit, main circuit main
module main (
  input  a,
  input  b,
  input  c
);

  wire NAND1_out, NAND2_out, NAND3_out, NAND4_out, NAND5_out, NAND6_out, NAND7_out, NAND8_out, NAND9_out,
       NAND10_out, not_1_out, not_2_out, not_3_out;

  not not_1 (not_1_out, a);
  not not_2 (not_2_out, b);
  not not_3 (not_3_out, c);
  nand NAND1 (NAND1_out, a, b);
  nand NAND2 (NAND2_out, a, c);
  nand NAND4 (NAND4_out, a, not_2_out, not_3_out);
  nand NAND5 (NAND5_out, not_1_out, b);
  nand NAND6 (NAND6_out, not_1_out, c);
  nand NAND8 (NAND8_out, b, c);
  nand NAND9 (NAND9_out, not_2_out, not_3_out);
  nand NAND3 (NAND3_out, NAND1_out, NAND2_out);
  nand NAND7 (NAND7_out, NAND4_out, NAND5_out, NAND6_out);
  nand NAND10 (NAND10_out, NAND8_out, NAND9_out);
  LED y3 (.in(NAND3_out));
  LED y2 (.in(NAND7_out));
  LED y1 (.in(NAND10_out));
  LED y0 (.in(not_3_out));
endmodule
