// Logisim project schem2.circ as structural Verilog: 1 circuit, main circuit main
module main (
  input  a,
  input  b,
  input  c
);

  wire NAND1_out, NAND2_out, NAND3_out, NAND4_out, NAND5_out, NAND6_out, NAND7_out, NAND8_out, NAND9_out,
       NAND10_out, NAND11_out, NAND12_out, NAND13_out, not_1_out, not_2_out, not_3_out;

  not not_1 (not_1_out, a);
  not not_2 (not_2_out, b);
  not not_3 (not_3_out, c);
  nand NAND1 (NAND1_out, not_2_out, c);
  nand NAND2 (NAND2_out, b, not_3_out);
  nand NAND5 (NAND5_out, b, c);
  nand NAND6 (NAND6_out, not_2_out, not_3_out);
  nand NAND10 (NAND10_out, not_1_out, b);
  nand NAND11 (NAND11_out, a, not_2_out);
  nand NAND3 (NAND3_out, NAND1_out, NAND2_out);
  nand NAND7 (NAND7_out, NAND5_out, NAND6_out);
  nand NAND12 (NAND12_out, NAND11_out, c);
  nand NAND4 (NAND4_out, not_1_out, NAND3_out);
  nand NAND8 (NAND8_out, a, NAND7_out);
  nand NAND13 (NAND13_out, NAND10_out, NAND12_out);
  nand NAND9 (NAND9_out, NAND4_out, NAND8_out);
  LED Di (.in(NAND9_out));
  LED Ci_1 (.in(NAND13_out));
endmodule
