// Logisim project schem.circ as structural Verilog: 1 circuit, main circuit main
module main (
  input  A
);

  wire clk_out, j_k_ff_1_q, j_k_ff_2_q, j_k_ff_2_qn, j_k_ff_3_q, j_k_ff_3_qn, NAND0_out, nand_1_out,
       nand_2_out, nand_3_out, nand_4_out, nand_5_out, not_1_out;

  not not_1 (not_1_out, A);
  nand nand_1 (nand_1_out, A, j_k_ff_2_qn, j_k_ff_3_qn);
  nand nand_2 (nand_2_out, not_1_out, j_k_ff_2_q, j_k_ff_3_q);
  nand nand_3 (nand_3_out, not_1_out, j_k_ff_3_q);
  nand nand_4 (nand_4_out, A, j_k_ff_3_qn);
  nand NAND0 (NAND0_out, nand_1_out, nand_2_out);
  Button clk (.out(clk_out));
  nand nand_5 (nand_5_out, nand_3_out, nand_4_out);
  J_K_Flip_Flop j_k_ff_1 (.J(NAND0_out), .clk(clk_out), .K(NAND0_out), .Q(j_k_ff_1_q));  // open: Qn, preset, en, reset
  J_K_Flip_Flop j_k_ff_2 (
    .J(nand_5_out), .clk(clk_out), .K(nand_5_out), .Q(j_k_ff_2_q), .Qn(j_k_ff_2_qn));  // open: preset, en, reset
  J_K_Flip_Flop j_k_ff_3 (
    .J(1'b1), .clk(clk_out), .K(1'b1), .Q(j_k_ff_3_q), .Qn(j_k_ff_3_qn));  // open: preset, en, reset
  LED Q0 (.in(j_k_ff_3_q));
  LED Q1 (.in(j_k_ff_2_q));
  LED Q2 (.in(j_k_ff_1_q));
endmodule
