// Logisim project schem2.circ as structural Verilog: 1 circuit, main circuit main
module main (
);

  wire clk_out, j_k_ff_1_q, j_k_ff_1_qn, j_k_ff_2_q, j_k_ff_2_qn, j_k_ff_3_q, j_k_ff_3_qn, j_k_ff_4_qn,
       nand_1_out, not_1_out, undriven;

  Button clk (.out(clk_out));
  LED Q3 (.in(j_k_ff_4_qn));
  LED Q2 (.in(j_k_ff_3_qn));
  LED Q1 (.in(j_k_ff_2_qn));
  LED Q0 (.in(j_k_ff_1_qn));
  J_K_Flip_Flop j_k_ff_1 (
    .J(1'b1), .clk(clk_out), .K(1'b1), .Q(j_k_ff_1_q), .Qn(j_k_ff_1_qn), .reset(undriven));  // open: preset, en
  J_K_Flip_Flop j_k_ff_2 (
    .J(1'b1), .clk(j_k_ff_1_q), .K(1'b1), .Q(j_k_ff_2_q), .Qn(j_k_ff_2_qn), .reset(undriven));  // open: preset, en
  nand nand_1 (nand_1_out, j_k_ff_1_q, j_k_ff_2_q, j_k_ff_3_qn);
  J_K_Flip_Flop j_k_ff_3 (
    .J(1'b1), .clk(j_k_ff_2_q), .K(1'b1), .Q(j_k_ff_3_q), .Qn(j_k_ff_3_qn), .reset(undriven));  // open: preset, en
  not not_1 (not_1_out, nand_1_out);
  J_K_Flip_Flop j_k_ff_4 (
    .J(1'b1), .clk(j_k_ff_3_q), .K(1'b1), .Qn(j_k_ff_4_qn), .reset(undriven));  // open: Q, preset, en
endmodule
