// Logisim project schem.circ as structural Verilog: 1 circuit, main circuit main
module main (
  input  mode
);

  wire clk_out, j_k_ff_1_q, j_k_ff_2_q, j_k_ff_2_qn, j_k_ff_3_q, j_k_ff_3_qn, NAND0_out, NAND1_out,
       NAND2_out, NAND3_out, NAND4_2_out, NAND4_out, not_1_out;

  Button clk (.out(clk_out));
  not not_1 (not_1_out, mode);
  nand NAND0 (NAND0_out, mode, j_k_ff_2_qn, j_k_ff_3_qn);
  nand NAND1 (NAND1_out, not_1_out, j_k_ff_2_q, j_k_ff_3_q);
  nand NAND3 (NAND3_out, not_1_out, j_k_ff_3_q);
  nand NAND4 (NAND4_out, mode, j_k_ff_3_qn);
  nand NAND2 (NAND2_out, NAND0_out, NAND1_out);
  nand NAND4_2 (NAND4_2_out, NAND3_out, NAND4_out);
  LED Q2 (.in(j_k_ff_1_q));
  J_K_Flip_Flop j_k_ff_1 (.J(NAND2_out), .clk(clk_out), .K(NAND2_out), .Q(j_k_ff_1_q));  // open: Qn, preset, en, reset
  LED Q1 (.in(j_k_ff_2_q));
  LED Q0 (.in(j_k_ff_3_q));
  J_K_Flip_Flop j_k_ff_2 (
    .J(NAND4_2_out), .clk(clk_out), .K(NAND4_2_out), .Q(j_k_ff_2_q), .Qn(j_k_ff_2_qn));  // open: preset, en, reset
  J_K_Flip_Flop j_k_ff_3 (
    .J(1'b1), .clk(clk_out), .K(1'b1), .Q(j_k_ff_3_q), .Qn(j_k_ff_3_qn));  // open: preset, en, reset
endmodule
