// Logisim project schem2.circ as structural Verilog: 1 circuit, main circuit main
module main (
  input  Mode
);

  wire clk_out, j_k_ff_1_q, j_k_ff_1_qn, j_k_ff_2_q, j_k_ff_2_qn, j_k_ff_3_q, j_k_ff_3_qn, j_k_ff_4_q,
       j_k_ff_4_qn, NAND1_out, NAND2_out, NAND3_out, not_1_out, not_2_out, XOR1_out, XOR2_out;

  Button clk (.out(clk_out));
  LED Q3 (.in(j_k_ff_4_qn));
  LED Q2 (.in(j_k_ff_3_qn));
  xor XOR2 (XOR2_out, clk_out, XOR1_out);
  LED Q1 (.in(j_k_ff_2_qn));
  LED Q0 (.in(j_k_ff_1_qn));
  J_K_Flip_Flop j_k_ff_1 (
    .J(1'b1), .clk(XOR2_out), .K(1'b1), .Q(j_k_ff_1_q), .Qn(j_k_ff_1_qn), .reset(XOR1_out));  // open: preset, en
  J_K_Flip_Flop j_k_ff_2 (
    .J(1'b1), .clk(j_k_ff_1_q), .K(1'b1), .Q(j_k_ff_2_q), .Qn(j_k_ff_2_qn), .reset(XOR1_out));  // open: preset, en
  not not_1 (not_1_out, Mode);
  nand NAND2 (NAND2_out, j_k_ff_4_qn, j_k_ff_2_qn, j_k_ff_1_qn, Mode);
  nand NAND1 (NAND1_out, not_1_out, j_k_ff_3_qn, j_k_ff_4_q);
  J_K_Flip_Flop j_k_ff_3 (
    .J(1'b1), .clk(j_k_ff_2_q), .K(1'b1), .Q(j_k_ff_3_q), .Qn(j_k_ff_3_qn), .reset(XOR1_out));  // open: preset, en
  not not_2 (not_2_out, NAND2_out);
  nand NAND3 (NAND3_out, not_2_out, j_k_ff_3_q);
  J_K_Flip_Flop j_k_ff_4 (
    .J(1'b1), .clk(j_k_ff_3_q), .K(1'b1), .Q(j_k_ff_4_q), .Qn(j_k_ff_4_qn), .reset(XOR1_out));  // open: preset, en
  xor XOR1 (XOR1_out, NAND3_out, NAND1_out);
endmodule
