// Logisim project schem2v2.circ as structural Verilog: 1 circuit, main circuit main
module main (
);

  wire button_1_out, button_2_out, dipswitch_1_sw8, j_k_ff_1_q, j_k_ff_2_q, j_k_ff_2_qn, j_k_ff_3_q,
       j_k_ff_3_qn, j_k_ff_4_q, j_k_ff_4_qn, j_k_ff_5_q, j_k_ff_5_qn, nand_1_out, nand_2_out, nand_3_out,
       nor_1_out, not_1_out, not_2_out, not_3_out, xor_1_out, xor_2_out;

  DipSwitch dipswitch_1 (.sw8(dipswitch_1_sw8));  // open: sw1, sw2, sw3, sw4, sw5, sw6, sw7
  Button button_1 (.out(button_1_out));
  Button button_2 (.out(button_2_out));
  xor xor_1 (xor_1_out, button_1_out, not_3_out);
  J_K_Flip_Flop j_k_ff_1 (
    .J(dipswitch_1_sw8), .K(dipswitch_1_sw8), .clk(button_2_out), .Q(j_k_ff_1_q));  // open: Qn, preset, reset
  LED led_1 (.in(j_k_ff_5_qn));
  J_K_Flip_Flop j_k_ff_2 (
    .J(dipswitch_1_sw8), .K(dipswitch_1_sw8), .clk(xor_1_out), .Q(j_k_ff_2_q), .Qn(j_k_ff_2_qn),
    .reset(not_3_out));  // open: preset
  LED led_2 (.in(j_k_ff_4_qn));
  LED led_3 (.in(j_k_ff_3_qn));
  LED led_4 (.in(j_k_ff_2_qn));
  not not_1 (not_1_out, j_k_ff_1_q);
  J_K_Flip_Flop j_k_ff_3 (
    .J(dipswitch_1_sw8), .K(dipswitch_1_sw8), .clk(j_k_ff_2_q), .Q(j_k_ff_3_q), .Qn(j_k_ff_3_qn),
    .reset(not_3_out));  // open: preset
  J_K_Flip_Flop j_k_ff_4 (
    .J(dipswitch_1_sw8), .K(dipswitch_1_sw8), .clk(j_k_ff_3_q), .Q(j_k_ff_4_q), .Qn(j_k_ff_4_qn),
    .reset(not_3_out));  // open: preset
  nand nand_1 (nand_1_out, j_k_ff_5_qn, j_k_ff_3_qn, j_k_ff_2_qn, j_k_ff_1_q);
  nand nand_2 (nand_2_out, not_1_out, j_k_ff_4_qn, j_k_ff_5_q);
  not not_2 (not_2_out, nand_1_out);
  nand nand_3 (nand_3_out, not_2_out, j_k_ff_4_q);
  J_K_Flip_Flop j_k_ff_5 (
    .J(dipswitch_1_sw8), .K(dipswitch_1_sw8), .clk(j_k_ff_4_q), .Q(j_k_ff_5_q), .Qn(j_k_ff_5_qn),
    .reset(not_3_out));  // open: preset
  xor xor_2 (xor_2_out, nand_3_out, nand_2_out);
  not not_3 (not_3_out, nor_1_out);
  nor nor_1 (nor_1_out, xor_2_out, button_2_out);
endmodule
