// Logisim project schem2v3(final).circ as structural Verilog: 1 circuit, main circuit main
module main (
  input  in_1,
  input  mode
);

  wire clock_out, j_k_ff_1_q, j_k_ff_1_qn, j_k_ff_2_q, j_k_ff_2_qn, j_k_ff_3_q, j_k_ff_3_qn, j_k_ff_4_q,
       j_k_ff_4_qn, nand_1_out, nand_2_out, nand_3_out, nand_4_out, nand_5_out, not_1_out;

  LED Q3 (.in(j_k_ff_4_q));
  LED Q2 (.in(j_k_ff_3_q));
  Button clock (.out(clock_out));
  LED Q1 (.in(j_k_ff_2_q));
  LED Q0 (.in(j_k_ff_1_q));
  J_K_Flip_Flop j_k_ff_1 (
    .J(in_1), .K(in_1), .clk(clock_out), .Q(j_k_ff_1_q), .Qn(j_k_ff_1_qn), .reset(not_1_out));  // open: preset
  J_K_Flip_Flop j_k_ff_2 (
    .J(in_1), .K(in_1), .clk(j_k_ff_1_qn), .Q(j_k_ff_2_q), .Qn(j_k_ff_2_qn), .reset(not_1_out));  // open: preset
  J_K_Flip_Flop j_k_ff_3 (
    .J(in_1), .K(in_1), .clk(j_k_ff_2_qn), .Q(j_k_ff_3_q), .Qn(j_k_ff_3_qn), .reset(not_1_out));  // open: preset
  J_K_Flip_Flop j_k_ff_4 (
    .J(in_1), .K(in_1), .clk(j_k_ff_3_qn), .Q(j_k_ff_4_q), .Qn(j_k_ff_4_qn), .reset(not_1_out));  // open: preset
  nand nand_1 (nand_1_out, j_k_ff_4_qn, j_k_ff_3_qn);
  nand nand_2 (nand_2_out, mode, j_k_ff_4_qn);
  nand nand_3 (nand_3_out, mode, j_k_ff_2_qn);
  nand nand_4 (nand_4_out, mode, j_k_ff_2_q, j_k_ff_1_qn);
  not not_1 (not_1_out, nand_5_out);
  nand nand_5 (nand_5_out, nand_1_out, nand_2_out, nand_3_out, nand_4_out);
endmodule
