// Logisim project schemv2.circ as structural Verilog: 1 circuit, main circuit main
module main (
  input  z1,
  input  z0
);

  wire clock_out, d_ff_1_q, d_ff_2_q, NAND1_out, NAND2_out, NAND3_out, NAND4_out, NAND5_out, NAND6_out,
       NAND7_out, NAND8_out, not_1_out, not_2_out, reset_out;

  not not_1 (not_1_out, z0);
  not not_2 (not_2_out, z1);
  nand NAND1 (NAND1_out, not_1_out, d_ff_1_q);
  nand NAND2 (NAND2_out, z1, d_ff_1_q);
  nand NAND3 (NAND3_out, z1, not_1_out);
  nand NAND5 (NAND5_out, not_2_out, z0);
  nand NAND6 (NAND6_out, not_2_out, d_ff_2_q);
  nand NAND7 (NAND7_out, z0, d_ff_2_q);
  nand NAND4 (NAND4_out, NAND1_out, NAND2_out, NAND3_out);
  Button clock (.out(clock_out));
  nand NAND8 (NAND8_out, NAND5_out, NAND6_out, NAND7_out);
  D_Flip_Flop d_ff_1 (.D(NAND4_out), .clk(clock_out), .Q(d_ff_1_q), .preset(reset_out));  // open: Qn, reset
  LED y1 (.in(NAND4_out));
  Button reset (.out(reset_out));
  LED y2 (.in(NAND8_out));
  D_Flip_Flop d_ff_2 (.D(NAND8_out), .clk(clock_out), .Q(d_ff_2_q), .preset(reset_out));  // open: Qn, reset
endmodule
