// Logisim project schem1.circ as structural Verilog: 1 circuit, main circuit main
module main (
);

  wire clk_out, j_k_ff_1_q, j_k_ff_1_qn, j_k_ff_2_q, j_k_ff_2_qn, NAND0_out, NAND1_out, NAND2_out, NOR0_out,
       NOR1_out, not_1_out, Z_out;

  Button clk (.out(clk_out));
  Button Z (.out(Z_out));
  nor NOR0 (NOR0_out, not_1_out, j_k_ff_2_q);
  not not_1 (not_1_out, Z_out);
  J_K_Flip_Flop j_k_ff_1 (
    .J(Z_out), .clk(clk_out), .K(NOR0_out), .Q(j_k_ff_1_q), .Qn(j_k_ff_1_qn));  // open: preset, en, reset
  nand NAND0 (NAND0_out, not_1_out, j_k_ff_1_qn, j_k_ff_2_q);
  nand NAND1 (NAND1_out, Z_out, j_k_ff_1_q, j_k_ff_2_qn);
  nor NOR1 (NOR1_out, j_k_ff_1_q, Z_out);
  nand NAND2 (NAND2_out, NAND0_out, NAND1_out);
  J_K_Flip_Flop j_k_ff_2 (
    .J(not_1_out), .clk(clk_out), .K(NOR1_out), .Q(j_k_ff_2_q), .Qn(j_k_ff_2_qn));  // open: preset, en, reset
  LED Y (.in(NAND2_out));
endmodule
