// Logisim project schem.circ as structural Verilog: 1 circuit, main circuit main
module main (
  input  E,
  input  E_2
);

  wire and_1_out, and_2_out, and_3_out, and_4_out, and_5_out, and_6_out, and_7_out, and_8_out, and_9_out,
       and_10_out, and_11_out, and_12_out, and_13_out, and_14_out, and_15_out, and_16_out, and_17_out,
       and_18_out, and_19_out, and_20_out, and_21_out, and_22_out, inp0_2_out, inp0_3_out, inp0_out,
       inp1_2_out, inp1_3_out, inp1_out, inp2_2_out, inp2_3_out, inp2_out, nand_1_out, nand_2_out,
       nand_3_out, nand_4_out, nand_5_out, nand_6_out, nand_7_out, nand_8_out, nand_9_out, nand_10_out,
       nand_11_out, nand_12_out, nand_13_out, nand_14_out, nand_15_out, nand_16_out, nand_17_out, nor_1_out,
       nor_2_out, nor_3_out, nor_4_out, nor_5_out, nor_6_out, nor_7_out, nor_8_out, nor_9_out, nor_10_out,
       nor_11_out, nor_12_out, nor_13_out, nor_14_out, nor_15_out, nor_16_out, nor_17_out, nor_18_out,
       nor_19_out, nor_20_out, nor_21_out, nor_22_out, nor_23_out, nor_24_out, nor_25_out, nor_26_out,
       nor_27_out, not_1_out, not_2_out, not_3_out, not_4_out, not_5_out, not_6_out, not_7_out, not_8_out,
       not_9_out, not_10_out, not_11_out, not_12_out, not_13_out, not_14_out, not_15_out, not_16_out,
       not_17_out, not_18_out, not_19_out, not_20_out, not_21_out, not_22_out, READ_2_out, READ_3_out,
       READ_out, RESET_2_out, RESET_3_out, RESET_out, s_r_ff_1_q, s_r_ff_2_q, s_r_ff_3_q, s_r_ff_3_qn,
       START_2_out, START_3_out, START_out;

  Button READ (.out(READ_out));
  Button inp2 (.out(inp2_out));
  Button inp1 (.out(inp1_out));
  Button inp0 (.out(inp0_out));
  Button START (.out(START_out));
  Button RESET (.out(RESET_out));
  Button READ_2 (.out(READ_2_out));
  Button inp2_2 (.out(inp2_2_out));
  Button inp1_2 (.out(inp1_2_out));
  Button inp0_2 (.out(inp0_2_out));
  Button START_2 (.out(START_2_out));
  Button RESET_2 (.out(RESET_2_out));
  Button READ_3 (.out(READ_3_out));
  Button inp2_3 (.out(inp2_3_out));
  Button inp1_3 (.out(inp1_3_out));
  Button inp0_3 (.out(inp0_3_out));
  Button START_3 (.out(START_3_out));
  Button RESET_3 (.out(RESET_3_out));
  and and_1 (and_1_out, not_5_out, inp0_out);
  and and_2 (and_2_out, START_out, nand_15_out);
  and and_3 (and_3_out, READ_2_out, E);
  and and_4 (and_4_out, inp2_2_out, E);
  and and_5 (and_5_out, not_6_out, inp0_2_out);
  and and_6 (and_6_out, START_2_out, nand_17_out);
  and and_7 (and_7_out, s_r_ff_1_q, inp0_3_out);
  and and_8 (and_8_out, START_3_out, s_r_ff_3_qn);
  nor nor_1 (nor_1_out, READ_out, inp2_out);
  not not_1 (not_1_out, inp1_out);
  nor nor_2 (nor_2_out, and_1_out, and_2_out);
  nand nand_1 (nand_1_out, nor_2_out, nand_2_out);
  nand nand_2 (nand_2_out, nand_1_out, nor_3_out);
  nor nor_3 (nor_3_out, RESET_out, not_14_out);
  nor nor_4 (nor_4_out, RESET_out, inp0_out);
  not not_2 (not_2_out, nor_4_out);
  nor nor_5 (nor_5_out, and_3_out, and_4_out);
  nand nand_3 (nand_3_out, E, inp1_2_out);
  nor nor_6 (nor_6_out, and_5_out, and_6_out);
  nand nand_4 (nand_4_out, nor_6_out, nand_5_out);
  nand nand_5 (nand_5_out, nand_4_out, nor_7_out);
  nor nor_7 (nor_7_out, RESET_2_out, not_15_out);
  nor nor_8 (nor_8_out, RESET_2_out, inp0_2_out);
  and and_9 (and_9_out, READ_3_out, E_2);
  nor nor_9 (nor_9_out, and_9_out, and_10_out);
  and and_10 (and_10_out, inp2_3_out, E_2);
  nand nand_6 (nand_6_out, E_2, inp1_3_out);
  nor nor_10 (nor_10_out, and_7_out, and_8_out);
  not not_3 (not_3_out, nor_10_out);
  S_R_Flip_Flop s_r_ff_1 (.Q(s_r_ff_1_q), .reset(not_4_out), .preset(not_3_out));  // open: S, R, clk, Qn
  not not_4 (not_4_out, nor_11_out);
  nor nor_11 (nor_11_out, RESET_3_out, s_r_ff_2_q);
  nor nor_12 (nor_12_out, RESET_3_out, inp0_3_out);
  not not_5 (not_5_out, nand_2_out);
  LED led_1 (.in(not_5_out));
  not not_6 (not_6_out, nand_5_out);
  not not_7 (not_7_out, nor_8_out);
  LED led_2 (.in(not_6_out));
  not not_8 (not_8_out, nor_12_out);
  LED led_3 (.in(s_r_ff_1_q));
  not not_9 (not_9_out, nor_1_out);
  nand nand_7 (nand_7_out, nor_1_out, not_1_out);
  and and_11 (and_11_out, nand_7_out, not_5_out);
  and and_12 (and_12_out, inp1_out, not_14_out);
  not not_10 (not_10_out, nor_5_out);
  nand nand_8 (nand_8_out, nor_5_out, nand_3_out);
  and and_13 (and_13_out, nand_8_out, not_6_out);
  and and_14 (and_14_out, inp1_2_out, not_15_out);
  not not_11 (not_11_out, nor_9_out);
  nand nand_9 (nand_9_out, nor_9_out, nand_6_out);
  nor nor_13 (nor_13_out, and_11_out, and_12_out);
  nor nor_14 (nor_14_out, not_2_out, not_18_out);
  nor nor_15 (nor_15_out, and_13_out, and_14_out);
  nor nor_16 (nor_16_out, not_7_out, not_19_out);
  and and_15 (and_15_out, nand_9_out, s_r_ff_1_q);
  and and_16 (and_16_out, inp1_3_out, s_r_ff_2_q);
  nor nor_17 (nor_17_out, not_8_out, s_r_ff_3_q);
  nand nand_10 (nand_10_out, nor_13_out, nand_11_out);
  nand nand_11 (nand_11_out, nand_10_out, nor_14_out);
  nand nand_12 (nand_12_out, nor_15_out, nand_13_out);
  nand nand_13 (nand_13_out, nand_12_out, nor_16_out);
  nor nor_18 (nor_18_out, and_15_out, and_16_out);
  not not_12 (not_12_out, nor_18_out);
  S_R_Flip_Flop s_r_ff_2 (.Q(s_r_ff_2_q), .reset(not_13_out), .preset(not_12_out));  // open: S, R, clk, Qn
  not not_13 (not_13_out, nor_17_out);
  not not_14 (not_14_out, nand_11_out);
  LED led_4 (.in(not_14_out));
  not not_15 (not_15_out, nand_13_out);
  LED led_5 (.in(not_15_out));
  LED led_6 (.in(s_r_ff_2_q));
  and and_17 (and_17_out, not_9_out, not_14_out);
  and and_18 (and_18_out, inp2_out, not_18_out);
  nor nor_19 (nor_19_out, not_2_out, inp1_out);
  nor nor_20 (nor_20_out, not_7_out, inp1_2_out);
  nor nor_21 (nor_21_out, not_8_out, inp1_3_out);
  nor nor_22 (nor_22_out, and_17_out, and_18_out);
  nand nand_14 (nand_14_out, nor_22_out, nand_15_out);
  nand nand_15 (nand_15_out, nand_14_out, nor_19_out);
  and and_19 (and_19_out, not_10_out, not_15_out);
  nor nor_23 (nor_23_out, and_19_out, and_20_out);
  and and_20 (and_20_out, inp2_2_out, not_19_out);
  nand nand_16 (nand_16_out, nor_23_out, nand_17_out);
  nand nand_17 (nand_17_out, nand_16_out, nor_20_out);
  and and_21 (and_21_out, not_11_out, s_r_ff_2_q);
  and and_22 (and_22_out, inp2_3_out, s_r_ff_3_q);
  not not_16 (not_16_out, nor_24_out);
  S_R_Flip_Flop s_r_ff_3 (
    .Q(s_r_ff_3_q), .reset(not_17_out), .Qn(s_r_ff_3_qn), .preset(not_16_out));  // open: S, R, clk
  not not_17 (not_17_out, nor_21_out);
  not not_18 (not_18_out, nand_15_out);
  LED led_7 (.in(not_18_out));
  not not_19 (not_19_out, nand_17_out);
  LED led_8 (.in(not_19_out));
  nor nor_24 (nor_24_out, and_21_out, and_22_out);
  LED led_9 (.in(s_r_ff_3_q));
  nor nor_25 (nor_25_out, READ_out, not_18_out);
  not not_20 (not_20_out, nor_25_out);
  nor nor_26 (nor_26_out, READ_2_out, not_19_out);
  nor nor_27 (nor_27_out, READ_3_out, s_r_ff_3_q);
  LED led_10 (.in(not_20_out));
  not not_21 (not_21_out, nor_26_out);
  LED led_11 (.in(not_21_out));
  LED led_12 (.in(not_22_out));
  not not_22 (not_22_out, nor_27_out);
endmodule
