// Logisim project schem.circ as structural Verilog: 1 circuit, main circuit main
module main (
);

  wire nand_1_out, nand_2_out, nand_3_out, nand_4_out, nand_5_out, not_1_out, not_2_out, not_3_out, Q1_out,
       Q2_out, X1_out, X2_out;

  Button X1 (.out(X1_out));
  Button X2 (.out(X2_out));
  not not_1 (not_1_out, X1_out);
  not not_2 (not_2_out, X2_out);
  not not_3 (not_3_out, Q1_out);
  nand nand_1 (nand_1_out, not_1_out, Q2_out);
  nand nand_2 (nand_2_out, X1_out, Q1_out);
  nand nand_3 (nand_3_out, not_1_out, not_2_out, Q2_out);
  nand nand_4 (nand_4_out, X1_out, not_2_out, not_3_out);
  nand nand_5 (nand_5_out, not_2_out, not_3_out, Q2_out);
  nand Q1 (Q1_out, not_2_out, nand_1_out, nand_2_out);
  nand Q2 (Q2_out, nand_3_out, nand_5_out);
  LED Q1_2 (.in(Q1_out));
  LED Q2_2 (.in(Q2_out));

  // Notes on the sheet:
  //   Y
endmodule
